// Logisim project 7_segment_display.circ as structural Verilog: 2 circuits, main circuit main
module main (
  input  [3:0] in_1
);

  wire decoder_1_bottom, decoder_1_bottomleft, decoder_1_bottomright, decoder_1_middle, decoder_1_top,
       decoder_1_topleft, decoder_1_topright;

  decoder decoder_1 (
    .bit3(in_1[3]), .bit2(in_1[2]), .bit1(in_1[1]), .bit0(in_1[0]), .top(decoder_1_top),
    .bottom(decoder_1_bottom), .topright(decoder_1_topright), .topleft(decoder_1_topleft),
    .bottomright(decoder_1_bottomright), .bottomleft(decoder_1_bottomleft), .middle(decoder_1_middle));
  _7_Segment_Display u_7_segment_display_1 (
    .g(decoder_1_middle), .f(decoder_1_topleft), .a(decoder_1_top), .b(decoder_1_topright),
    .e(decoder_1_bottomleft), .d(decoder_1_bottom), .c(decoder_1_bottomright));  // open: dp
endmodule

module decoder (
  input  bit3,
  input  bit2,
  input  bit1,
  input  bit0,
  output top,
  output bottom,
  output topright,
  output topleft,
  output bottomright,
  output bottomleft,
  output middle
);

  wire and_1_out, and_2_out, and_3_out, and_4_out, and_5_out, and_6_out, and_7_out, and_8_out, and_9_out,
       and_10_out, and_11_out, and_12_out, and_13_out, and_14_out, and_15_out, and_16_out, not_1_out,
       not_2_out, not_3_out, not_4_out, not_5_out, not_6_out, not_7_out, not_8_out, not_9_out, not_10_out,
       not_11_out, not_12_out, not_13_out, not_14_out, not_15_out, not_16_out, not_17_out, not_18_out,
       not_19_out, not_20_out, not_21_out;

  not not_1 (not_1_out, bit2);
  and and_1 (and_1_out, not_1_out, not_2_out);
  not not_2 (not_2_out, bit0);
  and and_2 (and_2_out, bit2, bit0);
  not not_3 (not_3_out, bit2);
  and and_3 (and_3_out, not_3_out, not_4_out);
  not not_4 (not_4_out, bit0);
  not not_5 (not_5_out, bit2);
  and and_4 (and_4_out, not_5_out, bit1);
  and and_5 (and_5_out, bit1, not_6_out);
  not not_6 (not_6_out, bit0);
  not not_7 (not_7_out, bit1);
  and and_6 (and_6_out, bit2, not_7_out, bit0);
  not not_8 (not_8_out, bit2);
  not not_9 (not_9_out, bit1);
  and and_7 (and_7_out, not_9_out, not_10_out);
  not not_10 (not_10_out, bit0);
  and and_8 (and_8_out, bit1, bit0);
  not not_11 (not_11_out, bit1);
  and and_9 (and_9_out, not_11_out, not_12_out);
  not not_12 (not_12_out, bit0);
  and and_10 (and_10_out, bit2, not_13_out);
  not not_13 (not_13_out, bit1);
  and and_11 (and_11_out, bit2, not_14_out);
  not not_14 (not_14_out, bit0);
  not not_15 (not_15_out, bit1);
  or or_1 (bottomright, not_15_out, bit0, bit2);
  not not_16 (not_16_out, bit2);
  and and_12 (and_12_out, not_16_out, not_17_out);
  not not_17 (not_17_out, bit0);
  and and_13 (and_13_out, bit1, not_18_out);
  not not_18 (not_18_out, bit0);
  not not_19 (not_19_out, bit2);
  and and_14 (and_14_out, not_19_out, bit1);
  and and_15 (and_15_out, bit2, not_20_out);
  not not_20 (not_20_out, bit1);
  and and_16 (and_16_out, bit2, not_21_out);
  not not_21 (not_21_out, bit0);
  or or_2 (top, and_1_out, bit1, and_2_out, bit3);
  or or_3 (bottom, and_3_out, and_4_out, and_5_out, and_6_out, bit3);
  or or_4 (topright, not_8_out, and_7_out, and_8_out);
  or or_5 (topleft, and_9_out, and_10_out, and_11_out, bit3);
  or or_6 (bottomleft, and_12_out, and_13_out);
  or or_7 (middle, and_14_out, and_15_out, and_16_out, bit3);
endmodule
