// Logisim project RISCV.circ as structural Verilog: 7 circuits, main circuit RISCV
module Inc4 (
  input  [31:0] A,
  output [31:0] S
);

  // Incrementer #(.width(30)) incrementer_1: pin names not known; wires that end beside it: A[31:2], S[31:2]

  assign S[1:0] = A[1:0];
endmodule

module SelectALUOpcode (
  input  b30,
  input  b13,
  input  b12,
  input  b11,
  input  b5,
  input  b4,
  output Op0,
  output Op1,
  output Op2,
  output Op3
);

  wire and_1_out, and_2_out, and_3_out, and_4_out;

  and and_1 (and_1_out, b12, b4);
  and and_2 (and_2_out, b30, b4, b5);
  and and_3 (and_3_out, b13, ~b30);  // AND_Gate
  and and_4 (and_4_out, b13, ~b5);  // AND_Gate
  or or_1 (Op1, b11, and_1_out);
  or or_2 (Op2, b13, and_2_out);
  or or_3 (Op3, and_3_out, and_4_out);

  assign Op0 = b11;
endmodule

module getSelectorBits (
  input  b1,
  input  b0,
  output s3,
  output s2,
  output s1,
  output s0
);

  wire not_1_out, not_2_out, not_3_out, not_4_out;

  and and_1 (s3, b1, b0);
  not not_1 (not_1_out, b0);
  not not_2 (not_2_out, b1);
  not not_3 (not_3_out, b1);
  not not_4 (not_4_out, b0);
  and and_2 (s2, b1, not_1_out);
  and and_3 (s1, not_2_out, b0);
  and and_4 (s0, not_3_out, not_4_out);
endmodule

module selectOutputByte (
  input  [31:0] D,
  input  [1:0] n,
  output [31:0] out_3
);

  wire [31:0] bit_extender_1_out, bit_extender_2_out, bit_extender_3_out, bit_extender_4_out;

  assign bit_extender_1_out = {{24{1'b0}}, D[31:24]};  // Bit_Extender bit_extender_1
  assign bit_extender_2_out = {{24{1'b0}}, D[23:16]};  // Bit_Extender bit_extender_2
  assign bit_extender_3_out = {{24{1'b0}}, D[15:8]};  // Bit_Extender bit_extender_3
  assign bit_extender_4_out = {{24{1'b0}}, D[7:0]};  // Bit_Extender bit_extender_4
  Multiplexer #(.select(2), .width(32), .enable("false")) multiplexer_1 (
    .in0(bit_extender_1_out), .in1(bit_extender_2_out), .in2(bit_extender_3_out), .in3(bit_extender_4_out),
    .out(out_3), .sel(n));
endmodule

module selectInputByte (
  input  [31:0] D,
  input  [1:0] n,
  output [31:0] out_3
);

  Multiplexer #(.select(2), .width(32), .enable("false")) multiplexer_1 (
    .in0({D[7:0], {24{1'b0}}}), .in1({{8{1'b0}}, D[7:0], {16{1'b0}}}), .in2({{16{1'b0}}, D[7:0], {8{1'b0}}}),
    .in3({{24{1'b0}}, D[7:0]}), .out(out_3), .sel(n));
endmodule

module RISCV (
);

  wire allzeros_1_out_2, and_1_out, and_2_out, and_3_out, clock_1_out, comparator_black_box_1_p4, nand_1_out,
       not_1_out, registerfile_1_p7;
  wire [3:0] getselectorbits_1_s3, multiplexer_3_out, selectaluopcode_1_op0;
  wire [11:0] multiplexer_1_out, risc_vprogramrom_1_p2;
  wire [31:0] alu_1_p2, alu_1_p5, bit_extender_1_out, bit_extender_2_out, inc4_1_s, multiplexer_4_out,
       multiplexer_5_out, multiplexer_6_out, multiplexer_7_out, ram_1_p7, register_1_q, registerfile_1_p1,
       registerfile_1_p8, selectinputbyte_1_out_3, selectoutputbyte_1_out_3;
  wire [31:12] risc_vprogramrom_1_p2_2;

  Clock clock_1 (.out(clock_1_out));
  Register #(.width(32)) register_1 (.D(inc4_1_s), .clk(clock_1_out), .Q(register_1_q));  // open: en, clr
  Inc4 inc4_1 (.A(register_1_q), .S(inc4_1_s));
  // RISC_VProgramROM risc_vprogramrom_1: pin names not known; wires that end beside it: register_1_q, {risc_vprogramrom_1_p2_2, risc_vprogramrom_1_p2}
  Multiplexer #(.width(12), .enable("false")) multiplexer_1 (
    .in0({risc_vprogramrom_1_p2_2[31:25], risc_vprogramrom_1_p2[11:7]}),
    .in1(risc_vprogramrom_1_p2_2[31:20]), .out(multiplexer_1_out), .sel(nand_1_out));
  nand nand_1 (nand_1_out, risc_vprogramrom_1_p2[5], ~risc_vprogramrom_1_p2[4]);  // NAND_Gate
  and and_1 (and_1_out, risc_vprogramrom_1_p2[5], risc_vprogramrom_1_p2[4]);
  assign bit_extender_1_out = {{20{multiplexer_1_out[11]}}, multiplexer_1_out};  // Bit_Extender bit_extender_1
  // RegisterFile registerfile_1: pin names not known; wires that end beside it: registerfile_1_p1, clock_1_out, nand_1_out, risc_vprogramrom_1_p2[11:7], risc_vprogramrom_1_p2_2[19:15], risc_vprogramrom_1_p2_2[24:20], registerfile_1_p7, registerfile_1_p8
  SelectALUOpcode selectaluopcode_1 (
    .b30(risc_vprogramrom_1_p2_2[30]), .b13(risc_vprogramrom_1_p2_2[14]), .b12(risc_vprogramrom_1_p2_2[13]),
    .b11(risc_vprogramrom_1_p2_2[12]), .b5(risc_vprogramrom_1_p2[5]), .b4(risc_vprogramrom_1_p2[4]),
    .Op0(selectaluopcode_1_op0[0]), .Op1(selectaluopcode_1_op0[1]), .Op2(selectaluopcode_1_op0[2]),
    .Op3(selectaluopcode_1_op0[3]));
  // ALU alu_1: pin names not known; wires that end beside it: registerfile_1_p7, alu_1_p2, selectaluopcode_1_op0, registerfile_1_p8[4:0], alu_1_p5
  Multiplexer #(.width(32), .enable("false")) multiplexer_2 (
    .in0(bit_extender_1_out), .in1(registerfile_1_p8), .out(alu_1_p2), .sel(and_1_out));
  // Comparator_Black_Box comparator_black_box_1: pin names not known; wires that end beside it: registerfile_1_p7, alu_1_p2, 1'b1, comparator_black_box_1_p4
  not not_1 (not_1_out, nand_1_out);
  assign bit_extender_2_out = {{31{1'b0}}, comparator_black_box_1_p4};  // Bit_Extender bit_extender_2
  Multiplexer #(.width(4), .enable("false")) multiplexer_3 (
    .in0(getselectorbits_1_s3), .in1(4'b1111), .out(multiplexer_3_out), .sel(risc_vprogramrom_1_p2_2[13]));
  getSelectorBits getselectorbits_1 (
    .b1(alu_1_p5[1]), .b0(alu_1_p5[0]), .s3(getselectorbits_1_s3[0]), .s2(getselectorbits_1_s3[1]),
    .s1(getselectorbits_1_s3[2]), .s0(getselectorbits_1_s3[3]));
  selectInputByte selectinputbyte_1 (.D(registerfile_1_p8), .n(alu_1_p5[1:0]), .out_3(selectinputbyte_1_out_3));
  Multiplexer #(.width(32), .enable("false")) multiplexer_4 (
    .in0(selectinputbyte_1_out_3), .in1(registerfile_1_p8), .out(multiplexer_4_out),
    .sel(risc_vprogramrom_1_p2_2[13]));
  and and_2 (and_2_out, not_1_out, allzeros_1_out_2);
  and and_3 (and_3_out, ~risc_vprogramrom_1_p2_2[14], risc_vprogramrom_1_p2_2[13], ~risc_vprogramrom_1_p2_2[12]);  // AND_Gate
  allZeros allzeros_1 (.in_1(alu_1_p5[31:22]), .out_2(allzeros_1_out_2));
  Multiplexer #(.width(32), .enable("false")) multiplexer_5 (
    .in0(alu_1_p5), .in1(bit_extender_2_out), .out(multiplexer_5_out), .sel(and_3_out));
  // RAM ram_1: pin names not known; wires that end beside it: alu_1_p5[21:2], multiplexer_4_out, and_2_out, multiplexer_3_out, clock_1_out, nand_1_out, ram_1_p7
  selectOutputByte selectoutputbyte_1 (.D(ram_1_p7), .n(alu_1_p5[1:0]), .out_3(selectoutputbyte_1_out_3));
  Multiplexer #(.width(32), .enable("false")) multiplexer_6 (
    .in0(selectoutputbyte_1_out_3), .in1(ram_1_p7), .out(multiplexer_6_out), .sel(risc_vprogramrom_1_p2_2[13]));
  Multiplexer #(.width(32), .enable("false")) multiplexer_7 (
    .in0(multiplexer_6_out), .in1(multiplexer_5_out), .out(multiplexer_7_out), .sel(risc_vprogramrom_1_p2[4]));
  Multiplexer #(.width(32), .enable("false")) multiplexer_8 (
    .in0(multiplexer_7_out), .in1({risc_vprogramrom_1_p2_2, {12{1'b0}}}), .out(registerfile_1_p1),
    .sel(risc_vprogramrom_1_p2[2]));

  // Notes on the sheet:
  //   contents of risc_vprogramrom_1 (hex, n*v repeats v):
  //   # Random cases (N=29) # testing that a store to 0x156(0x9ba451a8) does not "wrap around" addi x1,
  //   x0, 1 lui x2, 0x45 addi x2, x2, 0x1a8 sw x1, 0x156(x2) lui x2, 0x9ba45 addi x2, x2, 0x1a8 sw x0,
  //   0x156(x2) lui x2, 0x45 addi x2, x2, 0x1a8 lw x3, 0x156(x2) ## expect[3] = 1148965725 # testing that
  //   a store to 0x469(0x4da16824) does not "wrap around" addi x1, x0, 1 lui x2, 0x17 addi x2, x2, 0x824
  //   sw x1, 0x469(x2) lui x2, 0x4da17 addi x2, x2, 0x824 sw x0, 0x469(x2) lui x2, 0x17 addi x2, x2, 0x824
  //   lw x4, 0x469(x2) ## expect[4] = -2083035039 # testing that a store to 0xba3(0x96d5dfec) does not
  //   "wrap around" addi x1, x0, 1 lui x2, 0x5e addi x2, x2, 0xfec sw x1, 0xba3(x2) lui x2, 0x96d5e addi
  //   x2, x2, 0xfec sw x0, 0xba3(x2) lui x2, 0x5e addi x2, x2, 0xfec lw x5, 0xba3(x2) ## expect[5] =
  //   -375971340 # testing that a store to 0x6cf(0x4559c010) does not "wrap around" addi x1, x0, 1 lui x2,
  //   0x9c addi x2, x2, 0x10 sw x1, 0x6cf(x2) lui x2, 0x4559c addi x2, x2, 0x10 sw x0, 0x6cf(x2) lui x2,
  //   0x9c addi x2, x2, 0x10 lw x6, 0x6cf(x2) ## expect[6] = -1532657132 # testing that a store to
  //   0xc4c(0xad5401f8) does not "wrap around" addi x1, x0, 1 lui x2, 0x40 addi x2, x2, 0x1f8 sw x1,
  //   0xc4c(x2) lui x2, 0xad540 addi x2, x2, 0x1f8 sw x0, 0xc4c(x2) lui x2, 0x40 addi x2, x2, 0x1f8 lw x7,
  //   0xc4c(x2) ## expect[7] = -472999116 # testing that a store to 0xf5c(0xa96621f4) does not "wrap
  //   around" addi x1, x0, 1 lui x2, 0x62 addi x2, x2, 0x1f4 sw x1, 0xf5c(x2) lui x2, 0xa9662 addi x2, x2,
  //   0x1f4 sw x0, 0xf5c(x2) lui x2, 0x62 addi x2, x2, 0x1f4 lw x8, 0xf5c(x2) ## expect[8] = 1475194818 #
  //   testing that a store to 0xd1c(0x625b70a0) does not "wrap around" addi x1, x0, 1 lui x2, 0xb7 addi
  //   x2, x2, 0xa0 sw x1, 0xd1c(x2) lui x2, 0x625b7 addi x2, x2, 0xa0 sw x0, 0xd1c(x2) lui x2, 0xb7 addi
  //   x2, x2, 0xa0 lw x9, 0xd1c(x2) ## expect[9] = -427631631 # testing that a store to 0x359(0xf66a1130)
  //   does not "wrap around" addi x1, x0, 1 lui x2, 0xa1 addi x2, x2, 0x130 sw x1, 0x359(x2) lui x2,
  //   0xf66a1 addi x2, x2, 0x130 sw x0, 0x359(x2) lui x2, 0xa1 addi x2, x2, 0x130 lw x10, 0x359(x2) ##
  //   expect[10] = -1102839097 # testing that a store to 0xcd(0x25e41ae0) does not "wrap around" addi x1,
  //   x0, 1 lui x2, 0x42 addi x2, x2, 0xae0 sw x1, 0xcd(x2) lui x2, 0x25e42 addi x2, x2, 0xae0 sw x0,
  //   0xcd(x2) lui x2, 0x42 addi x2, x2, 0xae0 lw x11, 0xcd(x2) ## expect[11] = 505404610 # testing that a
  //   store to 0x9b8(0xfe128038) does not "wrap around" addi x1, x0, 1 lui x2, 0x28 addi x2, x2, 0x38 sw
  //   x1, 0x9b8(x2) lui x2, 0xfe128 addi x2, x2, 0x38 sw x0, 0x9b8(x2) lui x2, 0x28 addi x2, x2, 0x38 lw
  //   x12, 0x9b8(x2) ## expect[12] = -982425247 # testing that a store to 0x7b9(0x8c5525d8) does not "wrap
  //   around" addi x1, x0, 1 lui x2, 0x52 addi x2, x2, 0x5d8 sw x1, 0x7b9(x2) lui x2, 0x8c552 addi x2, x2,
  //   0x5d8 sw x0, 0x7b9(x2) lui x2, 0x52 addi x2, x2, 0x5d8 lw x13, 0x7b9(x2) ## expect[13] = 132749661 #
  //   testing that a store to 0xfce(0x38653d0c) does not "wrap around" addi x1, x0, 1 lui x2, 0x54 addi
  //   x2, x2, 0xd0c sw x1, 0xfce(x2) lui x2, 0x38654 addi x2, x2, 0xd0c sw x0, 0xfce(x2) lui x2, 0x54 addi
  //   x2, x2, 0xd0c lw x14, 0xfce(x2) ## expect[14] = 1015133326 # testing that a store to
  //   0xa4f(0xc5826564) does not "wrap around" addi x1, x0, 1 lui x2, 0x26 addi x2, x2, 0x564 sw x1,
  //   0xa4f(x2) lui x2, 0xc5826 addi x2, x2, 0x564 sw x0, 0xa4f(x2) lui x2, 0x26 addi x2, x2, 0x564 lw
  //   x15, 0xa4f(x2) ## expect[15] = -1102756409 # testing that a store to 0x9b(0x1a3b5090) does not "wrap
  //   around" addi x1, x0, 1 lui x2, 0xb5 addi x2, x2, 0x90 sw x1, 0x9b(x2) lui x2, 0x1a3b5 addi x2, x2,
  //   0x90 sw x0, 0x9b(x2) lui x2, 0xb5 addi x2, x2, 0x90 lw x16, 0x9b(x2) ## expect[16] = 928570185 #
  //   testing that a store to 0x7ce(0xd8028e0c) does not "wrap around" addi x1, x0, 1 lui x2, 0x29 addi
  //   x2, x2, 0xe0c sw x1, 0x7ce(x2) lui x2, 0xd8029 addi x2, x2, 0xe0c sw x0, 0x7ce(x2) lui x2, 0x29 addi
  //   x2, x2, 0xe0c lw x17, 0x7ce(x2) ## expect[17] = -500556235 # testing that a store to
  //   0x155(0xaf87bf58) does not "wrap around" addi x1, x0, 1 lui x2, 0x7c addi x2, x2, 0xf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
endmodule

module allZeros (
  input  [9:0] in_1,
  output out_2
);

  nor nor_1 (out_2, in_1[0], in_1[1], in_1[2], in_1[3], in_1[4], in_1[5], in_1[6], in_1[7], in_1[8], in_1[9]);
endmodule
