// Logisim project four_bit_full_adder.circ as structural Verilog: 2 circuits, main circuit main
module main (
  input  [3:0] A,
  input  [3:0] B,
  input  Cin,
  output Cout,
  output [3:0] S
);

  wire one_bit_adder_1_cout, one_bit_adder_2_cout, one_bit_adder_3_cout;

  one_bit_adder one_bit_adder_1 (.A(A[0]), .B(B[0]), .Cin(Cin), .Cout(one_bit_adder_1_cout), .S(S[0]));
  one_bit_adder one_bit_adder_2 (.A(A[1]), .B(B[1]), .Cin(one_bit_adder_1_cout), .Cout(one_bit_adder_2_cout), .S(S[1]));
  one_bit_adder one_bit_adder_3 (.A(A[2]), .B(B[2]), .Cin(one_bit_adder_2_cout), .Cout(one_bit_adder_3_cout), .S(S[2]));
  one_bit_adder one_bit_adder_4 (.A(A[2]), .B(B[2]), .Cin(one_bit_adder_2_cout), .Cout(one_bit_adder_3_cout), .S(S[2]));
  one_bit_adder one_bit_adder_5 (.A(A[3]), .B(B[3]), .Cin(one_bit_adder_3_cout), .Cout(Cout), .S(S[3]));
endmodule

module one_bit_adder (
  input  A,
  input  B,
  input  Cin,
  output Cout,
  output S
);

  wire and_1_out, and_2_out, xor_1_out;

  or or_1 (Cout, and_1_out, and_2_out);
  and and_1 (and_1_out, B, A);
  and and_2 (and_2_out, xor_1_out, Cin);
  xor xor_1 (xor_1_out, A, B);
  xor xor_2 (S, xor_1_out, Cin);
endmodule
