// Logisim project fsm_lab.circ as structural Verilog: 2 circuits, main circuit main
module main (
  input  MyIn,
  output Z
);

  wire clock_1_out;
  wire [1:0] State_q, sub_1_n0;

  Clock clock_1 (.out(clock_1_out));
  Register #(.width(2)) State (.D(sub_1_n0), .clk(clock_1_out), .Q(State_q));  // open: en, clr
  sub sub_1 (.S1(State_q[1]), .S0(State_q[0]), .I(MyIn), .N1(sub_1_n0[1]), .N0(sub_1_n0[0]), .Z(Z));

  // Notes on the sheet:
  //   S0
  //   S1
  //   N0
  //   N1
endmodule

module sub (
  input  S1,
  input  S0,
  input  I,
  output N1,
  output N0,
  output Z
);

  wire not_1_out;

  not not_1 (not_1_out, I);
  and and_1 (Z, S1, I);
  and and_2 (N1, S0, not_1_out);

  assign N0 = I;
endmodule
