// Logisim project leftshift32.circ as structural Verilog: 6 circuits, main circuit LeftShift32
module LeftShift32 (
  input  [31:0] B,
  input  [4:0] Sa,
  input  Cin,
  output [31:0] C
);

  wire [31:0] leftshift1_1_c, leftshift2_1_c, leftshift4_1_c, leftshift8_1_c;

  LeftShift1 leftshift1_1 (.B(B), .S(Sa[0]), .Cin(Cin), .C(leftshift1_1_c));
  LeftShift2 leftshift2_1 (.B(leftshift1_1_c), .S(Sa[1]), .Cin(Cin), .C(leftshift2_1_c));
  LeftShift4 leftshift4_1 (.B(leftshift2_1_c), .S(Sa[2]), .Cin(Cin), .C(leftshift4_1_c));
  LeftShift8 leftshift8_1 (.B(leftshift4_1_c), .S(Sa[3]), .Cin(Cin), .C(leftshift8_1_c));
  LeftShift16 leftshift16_1 (.B(leftshift8_1_c), .S(Sa[4]), .Cin(Cin), .C(C));
endmodule

module LeftShift1 (
  input  [31:0] B,
  input  S,
  input  Cin,
  output [31:0] C
);

  Multiplexer #(.width(32), .enable("false")) multiplexer_1 (.in0(B), .in1({B[30:0], Cin}), .out(C), .sel(S));
endmodule

module LeftShift2 (
  input  [31:0] B,
  input  S,
  input  Cin,
  output [31:0] C
);

  Multiplexer #(.width(32), .enable("false")) multiplexer_1 (.in0(B), .in1({B[29:0], {2{Cin}}}), .out(C), .sel(S));
endmodule

module LeftShift4 (
  input  [31:0] B,
  input  S,
  input  Cin,
  output [31:0] C
);

  Multiplexer #(.width(32), .enable("false")) multiplexer_1 (.in0(B), .in1({B[27:0], {4{Cin}}}), .out(C), .sel(S));
endmodule

module LeftShift8 (
  input  [31:0] B,
  input  S,
  input  Cin,
  output [31:0] C
);

  Multiplexer #(.width(32), .enable("false")) multiplexer_1 (.in0(B), .in1({B[23:0], {8{Cin}}}), .out(C), .sel(S));
endmodule

module LeftShift16 (
  input  [31:0] B,
  input  S,
  input  Cin,
  output [31:0] C
);

  Multiplexer #(.width(32), .enable("false")) multiplexer_1 (.in0(B), .in1({B[15:0], {16{Cin}}}), .out(C), .sel(S));
endmodule
