// Logisim project ALU.circ as structural Verilog: 17 circuits, main circuit ALU32
module Add32 (
  input  [31:0] A,
  input  [31:0] B,
  input  Cin,
  output V,
  output [31:0] C
);

  wire add1_1_cout, add1_2_cout, add2_1_cout, add4_1_cout, add8_1_cout, add16_1_cout;

  Add16 add16_1 (.A(A[15:0]), .B(B[15:0]), .Cin(Cin), .Cout(add16_1_cout), .S(C[15:0]));
  Add8 add8_1 (.A(A[23:16]), .B(B[23:16]), .Cin(add16_1_cout), .Cout(add8_1_cout), .S(C[23:16]));
  Add4 add4_1 (.A(A[27:24]), .B(B[27:24]), .Cin(add8_1_cout), .Cout(add4_1_cout), .S(C[27:24]));
  Add2 add2_1 (.A(A[29:28]), .B(B[29:28]), .Cin(add4_1_cout), .Cout(add2_1_cout), .S(C[29:28]));
  Add1 add1_1 (.A(A[30]), .B(B[30]), .Cin(add2_1_cout), .S(C[30]), .Cout(add1_1_cout));
  Add1 add1_2 (.A(A[31]), .B(B[31]), .Cin(add1_1_cout), .S(C[31]), .Cout(add1_2_cout));
  xor xor_1 (V, add1_2_cout, add1_1_cout);

  // Notes on the sheet:
  //   32 bit signed adder
endmodule

module ALU32 (
  input  [31:0] A,
  input  [31:0] B,
  input  [3:0] Op,
  input  [4:0] Sa,
  output V,
  output [31:0] C
);

  wire addsub32_1_v;
  wire [31:0] addsub32_1_c, and_1_out, cmp32_1_c, leftrightshift32_1_c, multiplexer_1_out, multiplexer_2_out,
       multiplexer_3_out, multiplexer_4_out, multiplexer_5_out, multiplexer_6_out, multiplexer_7_out,
       nor_1_out, or_1_out, xor_1_out;

  assign and_1_out = A & B;  // AND_Gate and_1, 32 bits wide
  assign or_1_out = A | B;  // OR_Gate or_1, 32 bits wide
  LeftRightShift32 leftrightshift32_1 (.B(B), .left(Op[2]), .arith(Op[0]), .Sa(Sa), .C(leftrightshift32_1_c));
  AddSub32 addsub32_1 (.A(A), .B(B), .sub(Op[2]), .C(addsub32_1_c), .V(addsub32_1_v));
  Cmp32 cmp32_1 (.A(A), .B(B), .eq_gt(Op[0]), .le_gt(Op[1]), .C(cmp32_1_c));
  assign xor_1_out = A ^ B;  // XOR_Gate xor_1, 32 bits wide
  assign nor_1_out = ~(A | B);  // NOR_Gate nor_1, 32 bits wide
  Multiplexer #(.width(32), .enable("false")) multiplexer_1 (
    .in0(leftrightshift32_1_c), .in1(cmp32_1_c), .out(multiplexer_1_out), .sel(Op[1]));
  Multiplexer #(.width(32), .enable("false")) multiplexer_2 (
    .in0(or_1_out), .in1(and_1_out), .out(multiplexer_2_out), .sel(Op[0]));
  Multiplexer #(.width(32), .enable("false")) multiplexer_3 (
    .in0(xor_1_out), .in1(nor_1_out), .out(multiplexer_3_out), .sel(Op[0]));
  Multiplexer #(.width(32), .enable("false")) multiplexer_4 (
    .in0(cmp32_1_c), .in1(multiplexer_3_out), .out(multiplexer_4_out), .sel(Op[1]));
  Multiplexer #(.width(32), .enable("false")) multiplexer_5 (
    .in0(multiplexer_2_out), .in1(leftrightshift32_1_c), .out(multiplexer_5_out), .sel(Op[2]));
  Multiplexer #(.width(32), .enable("false")) multiplexer_6 (
    .in0(multiplexer_1_out), .in1(multiplexer_4_out), .out(multiplexer_6_out), .sel(Op[2]));
  Multiplexer #(.width(32), .enable("false")) multiplexer_7 (
    .in0(multiplexer_5_out), .in1(addsub32_1_c), .out(multiplexer_7_out), .sel(Op[1]));
  Multiplexer #(.width(32), .enable("false")) multiplexer_8 (
    .in0(multiplexer_6_out), .in1(multiplexer_7_out), .out(C), .sel(Op[3]));
  and and_2 (V, addsub32_1_v, Op[1], Op[3]);

  // Notes on the sheet:
  //   First we compute all of the needed values, then we use a tree of 1-bit MUXs to select the correct one
  //   Assert V if V=1 and we are executing a subtract/add
endmodule

module LeftShift32 (
  input  [31:0] B,
  input  [4:0] Sa,
  input  Cin,
  output [31:0] C
);

  wire [31:0] leftshift1_1_c, leftshift2_1_c, leftshift4_1_c, leftshift8_1_c;

  LeftShift1 leftshift1_1 (.B(B), .S(Sa[0]), .Cin(Cin), .C(leftshift1_1_c));
  LeftShift2 leftshift2_1 (.B(leftshift1_1_c), .S(Sa[1]), .Cin(Cin), .C(leftshift2_1_c));
  LeftShift4 leftshift4_1 (.B(leftshift2_1_c), .S(Sa[2]), .Cin(Cin), .C(leftshift4_1_c));
  LeftShift8 leftshift8_1 (.B(leftshift4_1_c), .S(Sa[3]), .Cin(Cin), .C(leftshift8_1_c));
  LeftShift16 leftshift16_1 (.B(leftshift8_1_c), .S(Sa[4]), .Cin(Cin), .C(C));

  // Notes on the sheet:
  //   32 bit left shifter
endmodule

module LeftShift1 (
  input  [31:0] B,
  input  S,
  input  Cin,
  output [31:0] C
);

  Multiplexer #(.width(32), .enable("false")) multiplexer_1 (.in0(B), .in1({B[30:0], Cin}), .out(C), .sel(S));
endmodule

module LeftShift2 (
  input  [31:0] B,
  input  S,
  input  Cin,
  output [31:0] C
);

  Multiplexer #(.width(32), .enable("false")) multiplexer_1 (.in0(B), .in1({B[29:0], {2{Cin}}}), .out(C), .sel(S));
endmodule

module LeftShift4 (
  input  [31:0] B,
  input  S,
  input  Cin,
  output [31:0] C
);

  Multiplexer #(.width(32), .enable("false")) multiplexer_1 (.in0(B), .in1({B[27:0], {4{Cin}}}), .out(C), .sel(S));
endmodule

module LeftShift8 (
  input  [31:0] B,
  input  S,
  input  Cin,
  output [31:0] C
);

  Multiplexer #(.width(32), .enable("false")) multiplexer_1 (.in0(B), .in1({B[23:0], {8{Cin}}}), .out(C), .sel(S));
endmodule

module LeftShift16 (
  input  [31:0] B,
  input  S,
  input  Cin,
  output [31:0] C
);

  Multiplexer #(.width(32), .enable("false")) multiplexer_1 (.in0(B), .in1({B[15:0], {16{Cin}}}), .out(C), .sel(S));
endmodule

module Add1 (
  input  A,
  input  B,
  input  Cin,
  output S,
  output Cout
);

  wire and_1_out, and_2_out, and_3_out, and_4_out, and_5_out, and_6_out, and_7_out, not_1_out, not_2_out,
       not_3_out, not_4_out, not_5_out, not_6_out;

  not not_1 (not_1_out, A);
  not not_2 (not_2_out, B);
  not not_3 (not_3_out, A);
  not not_4 (not_4_out, Cin);
  not not_5 (not_5_out, B);
  not not_6 (not_6_out, Cin);
  and and_1 (and_1_out, B, Cin);
  and and_2 (and_2_out, A, Cin);
  and and_3 (and_3_out, A, B);
  and and_4 (and_4_out, not_1_out, not_2_out, Cin);
  and and_5 (and_5_out, not_3_out, B, not_4_out);
  and and_6 (and_6_out, A, not_5_out, not_6_out);
  and and_7 (and_7_out, A, B, Cin);
  or or_1 (Cout, and_1_out, and_2_out, and_3_out);
  or or_2 (S, and_4_out, and_5_out, and_6_out, and_7_out);

  // Notes on the sheet:
  //   This circuit was generated by Logism from a truth table
endmodule

module Add2 (
  input  [1:0] A,
  input  [1:0] B,
  input  Cin,
  output Cout,
  output [1:0] S
);

  wire add1_1_cout;

  Add1 add1_1 (.A(A[0]), .B(B[0]), .Cin(Cin), .S(S[0]), .Cout(add1_1_cout));
  Add1 add1_2 (.A(A[1]), .B(B[1]), .Cin(add1_1_cout), .S(S[1]), .Cout(Cout));
endmodule

module Add4 (
  input  [3:0] A,
  input  [3:0] B,
  input  Cin,
  output Cout,
  output [3:0] S
);

  wire add2_1_cout;

  Add2 add2_1 (.A(A[1:0]), .B(B[1:0]), .Cin(Cin), .Cout(add2_1_cout), .S(S[1:0]));
  Add2 add2_2 (.A(A[3:2]), .B(B[3:2]), .Cin(add2_1_cout), .Cout(Cout), .S(S[3:2]));
endmodule

module Add8 (
  input  [7:0] A,
  input  [7:0] B,
  input  Cin,
  output Cout,
  output [7:0] S
);

  wire add4_1_cout;

  Add4 add4_1 (.A(A[3:0]), .B(B[3:0]), .Cin(Cin), .Cout(add4_1_cout), .S(S[3:0]));
  Add4 add4_2 (.A(A[7:4]), .B(B[7:4]), .Cin(add4_1_cout), .Cout(Cout), .S(S[7:4]));
endmodule

module Add16 (
  input  [15:0] A,
  input  [15:0] B,
  input  Cin,
  output Cout,
  output [15:0] S
);

  wire add8_1_cout;

  Add8 add8_1 (.A(A[7:0]), .B(B[7:0]), .Cin(Cin), .Cout(add8_1_cout), .S(S[7:0]));
  Add8 add8_2 (.A(A[15:8]), .B(B[15:8]), .Cin(add8_1_cout), .Cout(Cout), .S(S[15:8]));
endmodule

module LeftRightShift32 (
  input  [31:0] B,
  input  left,
  input  arith,
  input  [4:0] Sa,
  output [31:0] C
);

  wire and_1_out;
  wire [31:0] leftshift32_1_c, multiplexer_1_out, rev32_1_b, rev32_2_b;

  Rev32 rev32_1 (.A(B), .B(rev32_1_b));
  Multiplexer #(.width(32), .enable("false")) multiplexer_1 (
    .in0(rev32_1_b), .in1(B), .out(multiplexer_1_out), .sel(left));
  and and_1 (and_1_out, ~left, B[31], arith);  // AND_Gate
  LeftShift32 leftshift32_1 (.B(multiplexer_1_out), .Sa(Sa), .Cin(and_1_out), .C(leftshift32_1_c));
  Rev32 rev32_2 (.A(leftshift32_1_c), .B(rev32_2_b));
  Multiplexer #(.width(32), .enable("false")) multiplexer_2 (
    .in0(rev32_2_b), .in1(leftshift32_1_c), .out(C), .sel(left));

  // Notes on the sheet:
  //   Is this a left shift (2nd Op bit)
  //   Is this an arithmatic shift (0th Op bit)
  //   Select the reverse of B if we are doing a right shift
  //   If we are doing a right arithmatic shift let Cin=the sign bit of B 
  //   Reverse the output again if we are doing a right shift
endmodule

module Rev32 (
  input  [31:0] A,
  output [31:0] B
);


  assign B = {A[0], A[1], A[2], A[3], A[4], A[5], A[6], A[7], A[8], A[9], A[10], A[11], A[12], A[13], A[14], A[15], A[16], A[17], A[18], A[19], A[20], A[21], A[22], A[23], A[24], A[25], A[26], A[27], A[28], A[29], A[30], A[31]};

  // Notes on the sheet:
  //   Helper subcicuit to reverse the bits of A
endmodule

module AddSub32 (
  input  [31:0] A,
  input  [31:0] B,
  input  sub,
  output [31:0] C,
  output V
);

  wire [31:0] bit_extender_1_out, xor_1_out;

  assign bit_extender_1_out = {{31{sub}}, sub};  // Bit_Extender bit_extender_1
  assign xor_1_out = B ^ bit_extender_1_out;  // XOR_Gate xor_1, 32 bits wide
  Add32 add32_1 (.A(A), .B(xor_1_out), .Cin(sub), .V(V), .C(C));

  // Notes on the sheet:
  //   Is this a subtraction (2nd Op bit)
  //   Invert B if sub=1
  //   Cin=sub
endmodule

module Cmp32 (
  input  [31:0] A,
  input  [31:0] B,
  input  eq_gt,
  input  le_gt,
  output [31:0] C
);

  wire multiplexer_2_out, or_1_out, or_2_out, xor_2_out;
  wire [31:0] multiplexer_1_out, xor_1_out;

  assign xor_1_out = A ^ B;  // XOR_Gate xor_1, 32 bits wide
  Multiplexer #(.width(32), .enable("false")) multiplexer_1 (
    .in0(xor_1_out), .in1(A), .out(multiplexer_1_out), .sel(le_gt));
  or or_1 (or_1_out, multiplexer_1_out[0], multiplexer_1_out[1], multiplexer_1_out[2], multiplexer_1_out[3], multiplexer_1_out[4], multiplexer_1_out[5], multiplexer_1_out[6], multiplexer_1_out[7], multiplexer_1_out[8], multiplexer_1_out[9], multiplexer_1_out[10], multiplexer_1_out[11], multiplexer_1_out[12], multiplexer_1_out[13], multiplexer_1_out[14], multiplexer_1_out[15], multiplexer_1_out[16], multiplexer_1_out[17], multiplexer_1_out[18], multiplexer_1_out[19], multiplexer_1_out[20], multiplexer_1_out[21], multiplexer_1_out[22], multiplexer_1_out[23], multiplexer_1_out[24], multiplexer_1_out[25], multiplexer_1_out[26], multiplexer_1_out[27], multiplexer_1_out[28], multiplexer_1_out[29], multiplexer_1_out[30], multiplexer_1_out[31]);
  or or_2 (or_2_out, ~or_1_out, A[31]);  // OR_Gate
  Multiplexer #(.enable("false")) multiplexer_2 (.in0(or_1_out), .in1(or_2_out), .out(multiplexer_2_out), .sel(le_gt));
  xor xor_2 (xor_2_out, multiplexer_2_out, eq_gt);
  assign C = {{31{1'b0}}, xor_2_out};  // Bit_Extender bit_extender_1

  // Notes on the sheet:
  //   Is this an eq or a gt (0th Op bit)
  //   Is this a le or a gt (1st Op bit)
  //   Extract the sign bit of A
  //   We want to see A nor B is 0 if we are doing a eq/ne but we want to see if A is 0 if we are doing an le/gt so we need a mux to select the input to the huge or gate
  //   Or all of the input bits together to see if a multi-bit signal is all 0's 
  //   Check if A is 0 and its sign bit is 1 (A <= 0) 
  //   If we are doing a le/gt select the or of A nor B (A != B), otherwise select A <= 0
  //   Negate the computed value if we are doing a eq/gt
  //   Extend the output to 32 bits
endmodule
